// Digital circuit piano.dig as structural Verilog
module piano (
  input  bntDo,
  input  btnRe,
  input  btnMi,
  input  btnFa,
  input  bntSol,
  input  btnLa,
  input  btnSi,
  input  CLK,
  output [7:0] Sonido
);

  wire btnDO, btnFA_t, btnLA_t, btnMI_t, btnRE_t, btnSI_t, btnSOL, HzDo, HzFa, HzLa, HzMi, HzRe, HzSi, HzSol,
       u_selectorNotes_outfq;
  wire [7:0] counter_8_out;
  wire [26:0] counter_1_out, counter_2_out, counter_3_out, counter_4_out, counter_5_out, counter_6_out,
       counter_7_out;

  Counter #(.Bits(27)) counter_1 (.en(1'b1), .C(CLK), .clr(HzDo), .out(counter_1_out));  // open: ovf
  Counter #(.Bits(27)) counter_2 (.en(1'b1), .C(CLK), .clr(HzRe), .out(counter_2_out));  // open: ovf
  Counter #(.Bits(27)) counter_3 (.en(1'b1), .C(CLK), .clr(HzMi), .out(counter_3_out));  // open: ovf
  Counter #(.Bits(27)) counter_4 (.en(1'b1), .C(CLK), .clr(HzFa), .out(counter_4_out));  // open: ovf
  Counter #(.Bits(27)) counter_5 (.en(1'b1), .C(CLK), .clr(HzSol), .out(counter_5_out));  // open: ovf
  Counter #(.Bits(27)) counter_6 (.en(1'b1), .C(CLK), .clr(HzLa), .out(counter_6_out));  // open: ovf
  Counter #(.Bits(27)) counter_7 (.en(1'b1), .C(CLK), .clr(HzSi), .out(counter_7_out));  // open: ovf
  Comparator #(.Bits(27)) comparator_1 (.a(27'h2ea), .b(counter_1_out), .eq(HzDo));  // open: gt, lt
  Comparator #(.Bits(27)) comparator_2 (.a(27'h298), .b(counter_2_out), .eq(HzRe));  // open: gt, lt
  Comparator #(.Bits(27)) comparator_3 (.a(27'h250), .b(counter_3_out), .eq(HzMi));  // open: gt, lt
  Comparator #(.Bits(27)) comparator_4 (.a(27'h22e), .b(counter_4_out), .eq(HzFa));  // open: gt, lt
  Comparator #(.Bits(27)) comparator_5 (.a(27'h1f1), .b(counter_5_out), .eq(HzSol));  // open: gt, lt
  Comparator #(.Bits(27)) comparator_6 (.a(27'h1bb), .b(counter_6_out), .eq(HzLa));  // open: gt, lt
  Comparator #(.Bits(27)) comparator_7 (.a(27'h18a), .b(counter_7_out), .eq(HzSi));  // open: gt, lt
  not not_1 (btnDO, bntDo);
  not not_2 (btnRE_t, btnRe);
  not not_3 (btnMI_t, btnMi);
  not not_4 (btnFA_t, btnFa);
  not not_5 (btnSOL, bntSol);
  not not_6 (btnLA_t, btnLa);
  not not_7 (btnSI_t, btnSi);
  selectorNotes #(.applicationType("IVERILOG")) u_selectorNotes (
    .notas({btnSI_t, btnLA_t, btnSOL, btnFA_t, btnMI_t, btnRE_t, btnDO}), .fq_DO(HzDo), .fq_RE(HzRe),
    .fq_MI(HzMi), .fq_FA(HzFa), .fq_SOL(HzSol), .fq_LA(HzLa), .fq_SI(HzSi), .clk(CLK),
    .outFq(u_selectorNotes_outfq));
  Counter #(.Bits(8)) counter_8 (.en(1'b1), .C(u_selectorNotes_outfq), .clr(1'b0), .out(counter_8_out));  // open: ovf
  ROM #(.AddrBits(8), .Bits(8)) ROM (.A(counter_8_out), .sel(1'b1), .D(Sonido));

  // Other names for the same wires on the sheet: notas[6:0] = {btnSI_t, btnLA_t, btnSOL, btnFA_t, btnMI_t, btnRE_t, btnDO}

  // Notes on the sheet:
  //   bntDo: pin M18
  //   btnRe: pin L18
  //   btnMi: pin M16
  //   btnFa: pin L17
  //   Sonido: pin H17,H18,J16,J18,K15,K16,L15,L16
  //   bntSol: pin K17
  //   btnLa: pin K18
  //   btnSi: pin C17
  //   CLK: pin V10
  //   board:MimasV2
  //   contents of ROM (hex, n*v repeats v):
  //   80,83,86,89,8c,8f,92,95,98,9c,9f,a2,a5,a8,ab,ae,b0,b3,b6,b9,bc,bf,c1,c4,c7,c9,cc,
  //   ce,d1,d3,d5,d8,da,dc,de,e0,e2,e4,e6,e8,ea,eb,ed,ef,f0,f2,f3,f4,f6,f7,f8,f9,fa,fb,
  //   fb,fc,fd,fd,fe,fe,fe,ff,ff,ff,ff,ff,ff,ff,fe,fe,fd,fd,fc,fc,fb,fa,f9,f8,f7,f6,f5,
  //   f4,f2,f1,ef,ee,ec,eb,e9,e7,e5,e3,e1,df,dd,db,d9,d7,d4,d2,cf,cd,ca,c8,c5,c3,c0,bd,
  //   ba,b8,b5,b2,af,ac,a9,a6,a3,a0,9d,9a,97,94,91,8e,8a,87,84,81,7e,7b,78,75,71,6e,6b,
  //   68,65,62,5f,5c,59,56,53,50,4d,4a,47,45,42,3f,3c,3a,37,35,32,30,2d,2b,28,26,24,22,
  //   20,1e,1c,1a,18,16,14,13,11,10,e,d,b,a,9,8,7,6,5,4,3,3,2,2,1,1,0,0,0,0,0,0,0,1,1,1,
  //   2,2,3,4,4,5,6,7,8,9,b,c,d,f,10,12,14,15,17,19,1b,1d,1f,21,23,25,27,2a,2c,2e,31,33,
  //   36,38,3b,3e,40,43,46,49,4c,4f,51,54,57,5a,5d,60,63,67,6a,6d,70,73,76,79,7c,7f
endmodule

/* Code of selectorNotes:
module selectorNotes(
    input [6:0] notas,
    input fq_DO,
    input fq_RE,
    input fq_MI,
    input fq_FA,
    input fq_SOL,
    input fq_LA,
    input fq_SI,
    input clk,
    output reg outFq
);


always @(posedge clk) begin
    if(notas[0]) begin
        outFq=fq_DO;
    end
    else if(notas[1])begin
        outFq=fq_RE;
    end
    else if(notas[2])begin
        outFq=fq_MI;
    end
    else if(notas[3])begin
        outFq=fq_FA;
    end
    else if(notas[4])begin
        outFq=fq_SOL;
    end
    else if(notas[5])begin
        outFq=fq_LA;
    end
    else if(notas[6])begin
        outFq=fq_SI;
    end
    else begin
        outFq=outFq;
    end
end
endmodule
*/
